// Logisim project saat.circ as structural Verilog: 1 circuit, main circuit main
module main (
);

  wire _0000_2_out, _0000_3_out, _0000_out, and_1_out, and_2_out, and_3_out, and_4_out, and_5_out, and_6_out,
       and_7_out, and_8_out, and_9_out, and_10_out, and_11_out, and_12_out, and_13_out, and_14_out,
       and_15_out, and_16_out, and_17_out, and_18_out, and_19_out, and_20_out, and_21_out, and_22_out,
       and_23_out, and_24_out, and_25_out, and_26_out, and_27_out, and_28_out, and_29_out, and_30_out,
       clock_1_out, clock_2_out, D1_2_q, D1_2_qn, D1_3_q, D1_3_qn, D1_q, D1_qn, D2_2_q, D2_2_qn, D2_3_q,
       D2_3_qn, D2_q, D2_qn, D3_2_q, D3_2_qn, D3_3_q, D3_3_qn, D3_q, D3_qn, D4_2_q, D4_2_qn, D4_3_q, D4_3_qn,
       D4_q, D4_qn, D5_2_q, D5_2_qn, D5_q, D5_qn, D6_2_q, D6_2_qn, D6_q, D6_qn, D7_2_q, D7_2_qn, D7_q, D7_qn,
       D11_q, D11_qn, D12_q, D12_qn, d_ff_1_q, L1_2_out, L1_3_out, L1_4_out, L1_5_out, L1_out, L2_2_out,
       L2_3_out, L2_4_out, L2_5_out, L2_out, L3_2_out, L3_3_out, L3_4_out, L3_5_out, L3_out, L4_2_out,
       L4_3_out, L4_4_out, L4_5_out, L4_out, L6_2_out, L6_3_out, L6_4_out, L6_5_out, L6_out, L7_2_out,
       L7_3_out, L7_4_out, L7_5_out, L7_out, L8_2_out, L8_3_out, L8_out, not_1_out, not_2_out, not_3_out,
       not_4_out, not_5_out, not_6_out, not_7_out, not_8_out, not_9_out, not_10_out, not_11_out, not_12_out,
       not_13_out, not_14_out, not_15_out, not_16_out, not_17_out, not_18_out, not_19_out, not_20_out,
       not_21_out, not_22_out, or_1_out, or_2_out, or_3_out, or_4_out, or_5_out, or_6_out, or_7_out,
       or_8_out, or_9_out, or_10_out, or_11_out, or_12_out, or_13_out, Q1_prime_Q2_prime_2_out,
       Q1_prime_Q2_prime_3_out, Q1_prime_Q2_prime_out, Q1_prime_Q3_2_out, Q1_prime_Q3_3_out, Q1_prime_Q3_out,
       Q1Q2_2_out, Q1Q2_3_out, Q1Q2_out, Q2Q1_prime_2_out, Q2Q1_prime_3_out, Q2Q1_prime_out,
       Q3_prime_Q1_prime_2_out, Q3_prime_Q1_prime_3_out, Q3_prime_Q1_prime_out, Q3_prime_Q2_2_out,
       Q3_prime_Q2_3_out, Q3_prime_Q2_out, Q3Q1_2_out, Q3Q1_3_out, Q3Q1_out, Q3Q2_2_out, Q3Q2_out,
       Q3Q2_prime_2_out, Q3Q2_prime_3_out, Q3Q2_prime_out, Q5_prime_Q6_2_out, Q5_prime_Q6_out,
       Q5_prime_Q6_prime_2_out, Q5_prime_Q6_prime_out, Q5_prime_Q7_2_out, Q5_prime_Q7_out,
       Q5_prime_Q7_prime_2_out, Q5_prime_Q7_prime_out, Q5Q6_2_out, Q5Q6_out, Q5Q7_2_out, Q5Q7_out;

  Clock clock_1 (.out(clock_1_out));
  D_Flip_Flop d_ff_1 (.clk(clock_1_out), .D(and_1_out), .Q(d_ff_1_q));  // open: Qn, preset, en, reset
  D_Flip_Flop D12 (.clk(_0000_out), .D(D11_q), .Q(D12_q), .Qn(D12_qn), .reset(d_ff_1_q));  // open: preset, en
  not not_1 (not_1_out, D2_q);
  not not_2 (not_2_out, D1_q);
  and and_1 (and_1_out, not_2_out, not_1_out, D3_q, not_3_out, not_4_out, D12_q);
  not not_3 (not_3_out, D4_q);
  or or_1 (or_1_out, and_3_out, and_4_out);
  not not_4 (not_4_out, D11_q);
  D_Flip_Flop D11 (.clk(_0000_out), .D(and_2_out), .Q(D11_q), .Qn(D11_qn), .reset(d_ff_1_q));  // open: preset, en
  and and_2 (and_2_out, D12_qn, D11_qn);
  not not_5 (not_5_out, D1_q);
  not not_6 (not_6_out, D2_q);
  and _0000 (_0000_out, not_5_out, not_6_out, not_7_out, not_8_out);
  not not_7 (not_7_out, D3_q);
  not not_8 (not_8_out, D4_q);
  D_Flip_Flop D4 (.clk(and_11_out), .D(or_1_out), .Q(D4_q), .Qn(D4_qn), .reset(and_1_out));  // open: preset, en
  and and_3 (and_3_out, D1_qn, D4_q);
  and and_4 (and_4_out, D3_q, D2_q, D1_q);
  _7_Segment_Display u_7_segment_display_1 (
    .g(D12_q), .f(and_2_out), .a(D11_qn), .b(1'b1), .e(D11_qn), .d(D11_qn), .c(D12_qn));  // open: dp
  and and_5 (and_5_out, D3_q, D2_qn);
  D_Flip_Flop D3 (.clk(and_11_out), .D(or_2_out), .Q(D3_q), .Qn(D3_qn), .reset(and_1_out));  // open: preset, en
  and Q3Q2 (Q3Q2_out, D3_q, D2_q);
  and Q1_prime_Q3 (Q1_prime_Q3_out, D3_q, D1_qn);
  or or_2 (or_2_out, and_5_out, and_6_out, and_7_out);
  and and_6 (and_6_out, D3_q, D1_qn);
  and and_7 (and_7_out, D3_qn, D1_q, D2_q);
  D_Flip_Flop D2 (.clk(and_11_out), .D(or_3_out), .Q(D2_q), .Qn(D2_qn), .reset(and_1_out));  // open: preset, en
  and Q3_prime_Q2 (Q3_prime_Q2_out, D3_qn, D2_q);
  and Q3Q2_prime (Q3Q2_prime_out, D3_q, D2_qn);
  and and_8 (and_8_out, D4_qn, D2_qn, D1_q);
  or or_3 (or_3_out, and_8_out, and_10_out);
  and Q3Q1 (Q3Q1_out, D3_q, D1_q);
  and Q2Q1_prime (Q2Q1_prime_out, D2_q, D1_qn);
  and Q1_prime_Q2_prime (Q1_prime_Q2_prime_out, D2_qn, D1_qn);
  and and_9 (and_9_out, D2_qn, Q3Q1_out);
  and Q1Q2 (Q1Q2_out, D2_q, D1_q);
  _7_Segment_Display u_7_segment_display_2 (
    .g(L4_out), .f(L3_out), .a(L2_out), .b(L1_out), .e(L8_out), .d(L7_out), .c(L6_out));  // open: dp
  D_Flip_Flop D1 (.clk(and_11_out), .D(D1_qn), .Q(D1_q), .Qn(D1_qn), .reset(and_1_out));  // open: preset, en
  and and_10 (and_10_out, D2_q, D1_qn);
  and Q3_prime_Q1_prime (Q3_prime_Q1_prime_out, D3_qn, D1_qn);
  or L8 (L8_out, Q3_prime_Q1_prime_out, Q2Q1_prime_out);
  or L7 (L7_out, Q2Q1_prime_out, Q3_prime_Q2_out, D4_q, Q3_prime_Q1_prime_out, and_9_out);
  or L6 (L6_out, D3_q, D2_qn, D1_q);
  or L4 (L4_out, Q3_prime_Q2_out, D4_q, Q3Q2_prime_out, Q2Q1_prime_out);
  or L3 (L3_out, Q1_prime_Q2_prime_out, Q3Q2_prime_out, D4_q, Q1_prime_Q3_out);
  or L2 (L2_out, Q3Q1_out, D4_q, D2_q, Q3_prime_Q1_prime_out);
  or L1 (L1_out, D3_qn, Q1_prime_Q2_prime_out, Q1Q2_out);
  not not_9 (not_9_out, D5_q);
  and and_11 (and_11_out, not_9_out, not_10_out, not_11_out);
  not not_10 (not_10_out, D6_q);
  not not_11 (not_11_out, D7_q);
  or or_4 (or_4_out, Q5Q6_out, Q5_prime_Q7_out);
  and Q5_prime_Q7 (Q5_prime_Q7_out, D5_qn, D7_q);
  D_Flip_Flop D7 (.clk(_0000_2_out), .D(or_4_out), .Q(D7_q), .Qn(D7_qn));  // open: preset, en, reset
  and and_12 (and_12_out, D7_qn, D6_qn, D5_q);
  and Q5_prime_Q7_prime (Q5_prime_Q7_prime_out, D7_qn, D5_qn);
  and Q5Q7 (Q5Q7_out, D7_q, D5_q);
  or L7_2 (L7_2_out, Q5Q7_out, Q5_prime_Q7_prime_out, D6_q);
  D_Flip_Flop D6 (.clk(_0000_2_out), .D(or_5_out), .Q(D6_q), .Qn(D6_qn));  // open: preset, en, reset
  or or_5 (or_5_out, and_12_out, Q5_prime_Q6_out);
  and Q5Q6 (Q5Q6_out, D6_q, D5_q);
  and Q5_prime_Q6_prime (Q5_prime_Q6_prime_out, D5_qn, D6_qn);
  D_Flip_Flop D5 (.clk(_0000_2_out), .D(D5_qn), .Q(D5_q), .Qn(D5_qn));  // open: preset, en, reset
  and Q5_prime_Q6 (Q5_prime_Q6_out, D6_q, D5_qn);
  or L1_2 (L1_2_out, D7_qn, D5_qn, D6_q);
  or L2_2 (L2_2_out, D6_q, Q5_prime_Q7_prime_out, Q5Q7_out);
  or L3_2 (L3_2_out, D7_q, Q5_prime_Q6_prime_out);
  or L4_2 (L4_2_out, D7_q, D6_q);
  or L6_2 (L6_2_out, D5_q, D6_qn);
  and _0000_2 (_0000_2_out, not_12_out, not_13_out, not_14_out, not_15_out);
  and and_13 (and_13_out, D1_2_qn, D4_2_q);
  or or_6 (or_6_out, and_13_out, and_14_out);
  and and_14 (and_14_out, D3_2_q, D2_2_q, D1_2_q);
  _7_Segment_Display u_7_segment_display_3 (
    .g(L4_2_out), .f(L3_2_out), .a(L2_2_out), .b(L1_2_out), .e(Q5_prime_Q7_prime_out), .d(L7_2_out),
    .c(L6_2_out));  // open: dp
  not not_12 (not_12_out, D1_2_q);
  not not_13 (not_13_out, D2_2_q);
  not not_14 (not_14_out, D3_2_q);
  not not_15 (not_15_out, D4_2_q);
  D_Flip_Flop D4_2 (.clk(and_21_out), .D(or_6_out), .Q(D4_2_q), .Qn(D4_2_qn));  // open: preset, en, reset
  D_Flip_Flop D3_2 (.clk(and_21_out), .D(or_7_out), .Q(D3_2_q), .Qn(D3_2_qn));  // open: preset, en, reset
  and Q3Q2_2 (Q3Q2_2_out, D3_2_q, D2_2_q);
  or or_7 (or_7_out, and_16_out, and_15_out, and_17_out);
  and and_15 (and_15_out, D3_2_q, D1_2_qn);
  and and_16 (and_16_out, D3_2_q, D2_2_qn);
  and and_17 (and_17_out, D3_2_qn, D1_2_q, D2_2_q);
  and Q3Q2_prime_2 (Q3Q2_prime_2_out, D3_2_q, D2_2_qn);
  and Q1_prime_Q3_2 (Q1_prime_Q3_2_out, D3_2_q, D1_2_qn);
  _7_Segment_Display u_7_segment_display_4 (
    .g(L4_3_out), .f(L3_3_out), .a(L2_3_out), .b(L1_3_out), .e(L8_2_out), .d(L7_3_out), .c(L6_3_out));  // open: dp
  D_Flip_Flop D2_2 (.clk(and_21_out), .D(or_8_out), .Q(D2_2_q), .Qn(D2_2_qn));  // open: preset, en, reset
  and Q3_prime_Q2_2 (Q3_prime_Q2_2_out, D3_2_qn, D2_2_q);
  and Q1_prime_Q2_prime_2 (Q1_prime_Q2_prime_2_out, D2_2_qn, D1_2_qn);
  and and_18 (and_18_out, D2_2_qn, Q3Q1_2_out);
  D_Flip_Flop D1_2 (.clk(and_21_out), .D(D1_2_qn), .Q(D1_2_q), .Qn(D1_2_qn));  // open: preset, en, reset
  and and_19 (and_19_out, D2_2_q, D1_2_qn);
  and and_20 (and_20_out, D4_2_qn, D2_2_qn, D1_2_q);
  or or_8 (or_8_out, and_20_out, and_19_out);
  and Q3Q1_2 (Q3Q1_2_out, D3_2_q, D1_2_q);
  and Q2Q1_prime_2 (Q2Q1_prime_2_out, D2_2_q, D1_2_qn);
  and Q3_prime_Q1_prime_2 (Q3_prime_Q1_prime_2_out, D3_2_qn, D1_2_qn);
  and Q1Q2_2 (Q1Q2_2_out, D2_2_q, D1_2_q);
  or L8_2 (L8_2_out, Q3_prime_Q1_prime_2_out, Q2Q1_prime_2_out);
  or L7_3 (L7_3_out, Q2Q1_prime_2_out, Q3_prime_Q2_2_out, D4_2_q, Q3_prime_Q1_prime_2_out, and_18_out);
  or L6_3 (L6_3_out, D3_2_q, D2_2_qn, D1_2_q);
  or L4_3 (L4_3_out, Q3_prime_Q2_2_out, D4_2_q, Q3Q2_prime_2_out, Q2Q1_prime_2_out);
  or L3_3 (L3_3_out, Q1_prime_Q2_prime_2_out, Q3Q2_prime_2_out, D4_2_q, Q1_prime_Q3_2_out);
  or L2_3 (L2_3_out, Q3Q1_2_out, D4_2_q, D2_2_q, Q3_prime_Q1_prime_2_out);
  or L1_3 (L1_3_out, D3_2_qn, Q1_prime_Q2_prime_2_out, Q1Q2_2_out);
  not not_16 (not_16_out, D5_2_q);
  not not_17 (not_17_out, D6_2_q);
  and and_21 (and_21_out, not_16_out, not_17_out, not_18_out);
  not not_18 (not_18_out, D7_2_q);
  or or_9 (or_9_out, Q5Q6_2_out, Q5_prime_Q7_2_out);
  and Q5_prime_Q7_2 (Q5_prime_Q7_2_out, D5_2_qn, D7_2_q);
  D_Flip_Flop D7_2 (.clk(_0000_3_out), .D(or_9_out), .Q(D7_2_q), .Qn(D7_2_qn));  // open: preset, en, reset
  and and_22 (and_22_out, D7_2_qn, D6_2_qn, D5_2_q);
  and Q5Q7_2 (Q5Q7_2_out, D7_2_q, D5_2_q);
  and Q5_prime_Q7_prime_2 (Q5_prime_Q7_prime_2_out, D7_2_qn, D5_2_qn);
  or L7_4 (L7_4_out, Q5Q7_2_out, Q5_prime_Q7_prime_2_out, D6_2_q);
  D_Flip_Flop D6_2 (.clk(_0000_3_out), .D(or_10_out), .Q(D6_2_q), .Qn(D6_2_qn));  // open: preset, en, reset
  or or_10 (or_10_out, and_22_out, Q5_prime_Q6_2_out);
  and Q5Q6_2 (Q5Q6_2_out, D6_2_q, D5_2_q);
  and Q5_prime_Q6_prime_2 (Q5_prime_Q6_prime_2_out, D5_2_qn, D6_2_qn);
  _7_Segment_Display u_7_segment_display_5 (
    .g(L4_4_out), .f(L3_4_out), .a(L2_4_out), .b(L1_4_out), .e(Q5_prime_Q7_prime_2_out), .d(L7_4_out),
    .c(L6_4_out));  // open: dp
  D_Flip_Flop D5_2 (.clk(_0000_3_out), .D(D5_2_qn), .Q(D5_2_q), .Qn(D5_2_qn));  // open: preset, en, reset
  and Q5_prime_Q6_2 (Q5_prime_Q6_2_out, D6_2_q, D5_2_qn);
  Clock clock_2 (.out(clock_2_out));
  or L1_4 (L1_4_out, D7_2_qn, D5_2_qn, D6_2_q);
  or L2_4 (L2_4_out, D6_2_q, Q5_prime_Q7_prime_2_out, Q5Q7_2_out);
  or L3_4 (L3_4_out, D7_2_q, Q5_prime_Q6_prime_2_out);
  or L4_4 (L4_4_out, D7_2_q, D6_2_q);
  or L6_4 (L6_4_out, D5_2_q, D6_2_qn);
  and _0000_3 (_0000_3_out, not_19_out, not_20_out, not_21_out, not_22_out);
  and and_23 (and_23_out, D1_3_qn, D4_3_q);
  or or_11 (or_11_out, and_23_out, and_24_out);
  and and_24 (and_24_out, D3_3_q, D2_3_q, D1_3_q);
  not not_19 (not_19_out, D1_3_q);
  not not_20 (not_20_out, D2_3_q);
  not not_21 (not_21_out, D3_3_q);
  not not_22 (not_22_out, D4_3_q);
  D_Flip_Flop D4_3 (.clk(clock_2_out), .D(or_11_out), .Q(D4_3_q), .Qn(D4_3_qn));  // open: preset, en, reset
  _7_Segment_Display u_7_segment_display_6 (
    .g(L4_5_out), .f(L3_5_out), .a(L2_5_out), .b(L1_5_out), .e(L8_3_out), .d(L7_5_out), .c(L6_5_out));  // open: dp
  D_Flip_Flop D3_3 (.clk(clock_2_out), .D(or_12_out), .Q(D3_3_q), .Qn(D3_3_qn));  // open: preset, en, reset
  // AND_Gate Q3Q2_3 has open pins: in0=D3_3_q, in1=D2_3_q, out=open
  or or_12 (or_12_out, and_25_out, and_26_out, and_27_out);
  and and_25 (and_25_out, D3_3_q, D2_3_qn);
  and and_26 (and_26_out, D3_3_q, D1_3_qn);
  and and_27 (and_27_out, D3_3_qn, D1_3_q, D2_3_q);
  and Q3Q2_prime_3 (Q3Q2_prime_3_out, D3_3_q, D2_3_qn);
  and Q1_prime_Q3_3 (Q1_prime_Q3_3_out, D3_3_q, D1_3_qn);
  D_Flip_Flop D2_3 (.clk(clock_2_out), .D(or_13_out), .Q(D2_3_q), .Qn(D2_3_qn));  // open: preset, en, reset
  and Q3_prime_Q2_3 (Q3_prime_Q2_3_out, D3_3_qn, D2_3_q);
  and Q1_prime_Q2_prime_3 (Q1_prime_Q2_prime_3_out, D2_3_qn, D1_3_qn);
  and and_28 (and_28_out, D2_3_qn, Q3Q1_3_out);
  D_Flip_Flop D1_3 (.clk(clock_2_out), .D(D1_3_qn), .Q(D1_3_q), .Qn(D1_3_qn));  // open: preset, en, reset
  and and_29 (and_29_out, D2_3_q, D1_3_qn);
  and and_30 (and_30_out, D4_3_qn, D2_3_qn, D1_3_q);
  or or_13 (or_13_out, and_30_out, and_29_out);
  and Q3Q1_3 (Q3Q1_3_out, D3_3_q, D1_3_q);
  and Q2Q1_prime_3 (Q2Q1_prime_3_out, D2_3_q, D1_3_qn);
  and Q3_prime_Q1_prime_3 (Q3_prime_Q1_prime_3_out, D3_3_qn, D1_3_qn);
  and Q1Q2_3 (Q1Q2_3_out, D2_3_q, D1_3_q);
  or L8_3 (L8_3_out, Q3_prime_Q1_prime_3_out, Q2Q1_prime_3_out);
  or L7_5 (L7_5_out, Q2Q1_prime_3_out, Q3_prime_Q2_3_out, D4_3_q, Q3_prime_Q1_prime_3_out, and_28_out);
  or L6_5 (L6_5_out, D3_3_q, D2_3_qn, D1_3_q);
  or L4_5 (L4_5_out, Q3_prime_Q2_3_out, D4_3_q, Q3Q2_prime_3_out, Q2Q1_prime_3_out);
  or L3_5 (L3_5_out, Q1_prime_Q2_prime_3_out, Q3Q2_prime_3_out, D4_3_q, Q1_prime_Q3_3_out);
  or L2_5 (L2_5_out, Q3Q1_3_out, D4_3_q, D2_3_q, Q3_prime_Q1_prime_3_out);
  or L1_5 (L1_5_out, D3_3_qn, Q1_prime_Q2_prime_3_out, Q1Q2_3_out);
endmodule
